// Logisim project cpu.circ as structural Verilog: 5 circuits, main circuit d-latch
module d_latch (
  input  enabler,
  input  \input ,
  output Q,
  output Q_prime
);

  wire and_1_out, and_2_out, not_1_out;

  not not_1 (not_1_out, \input );
  and and_1 (and_1_out, not_1_out, enabler);
  and and_2 (and_2_out, enabler, \input );
  nor nor_1 (Q, and_1_out, Q_prime);
  nor nor_2 (Q_prime, Q, and_2_out);
endmodule

module d_flip_flop (
  input  d,
  output q,
  output q_prime
);

  wire clk_out, d_latch_1_q_prime, not_1_out, not_2_out;

  Clock clk (.out(clk_out));
  d_latch d_latch_1 (.Q_prime(d_latch_1_q_prime), .\input (d), .enabler(not_1_out));  // open: Q
  not not_1 (not_1_out, clk_out);
  not not_2 (not_2_out, not_1_out);
  d_latch d_latch_2 (.Q(q), .Q_prime(q_prime), .\input (d_latch_1_q_prime), .enabler(not_2_out));
endmodule

module full_adder_1_bit (
  input  bit_1st,
  input  bit_2nd,
  input  carry_in,
  output carry_out,
  output result
);

  wire and_1_out, and_2_out, and_3_out;

  and and_1 (and_1_out, bit_1st, bit_2nd);
  and and_2 (and_2_out, bit_2nd, carry_in);
  and and_3 (and_3_out, bit_1st, carry_in);
  ExactlyOne xor_1 (.out(result), .in0(bit_1st), .in1(bit_2nd), .in2(carry_in));
  or or_1 (carry_out, and_1_out, and_2_out, and_3_out);
endmodule

module full_adder_4_bit (
  input  [3:0] input1,
  input  [3:0] input2,
  input  carry_in,
  output carry_out,
  output [3:0] \output 
);

  wire full_adder_1_bit_2_carry_out, full_adder_1_bit_3_carry_out, full_adder_1_bit_4_carry_out;

  full_adder_1_bit full_adder_1_bit_1 (
    .bit_1st(input1[3]), .bit_2nd(input2[3]), .carry_in(full_adder_1_bit_2_carry_out), .carry_out(carry_out),
    .result(\output [3]));
  full_adder_1_bit full_adder_1_bit_2 (
    .bit_1st(input1[2]), .bit_2nd(input2[2]), .carry_in(full_adder_1_bit_3_carry_out),
    .carry_out(full_adder_1_bit_2_carry_out), .result(\output [2]));
  full_adder_1_bit full_adder_1_bit_3 (
    .bit_1st(input1[1]), .bit_2nd(input2[1]), .carry_in(full_adder_1_bit_4_carry_out),
    .carry_out(full_adder_1_bit_3_carry_out), .result(\output [1]));
  full_adder_1_bit full_adder_1_bit_4 (
    .bit_1st(input1[0]), .bit_2nd(input2[0]), .carry_in(carry_in), .carry_out(full_adder_1_bit_4_carry_out),
    .result(\output [0]));
endmodule

module full_adder_16_bit (
  input  [15:0] in_1,
  input  [15:0] in_2,
  input  carry_in,
  output carry_out,
  output [15:0] \output 
);

  wire full_adder_4_bit_2_carry_out, full_adder_4_bit_3_carry_out, full_adder_4_bit_4_carry_out;

  full_adder_4_bit full_adder_4_bit_1 (
    .input1(in_1[15:12]), .input2(in_2[15:12]), .carry_in(full_adder_4_bit_2_carry_out),
    .carry_out(carry_out), .\output (\output [3:0]));
  full_adder_4_bit full_adder_4_bit_2 (
    .input1(in_1[11:8]), .input2(in_2[11:8]), .carry_in(full_adder_4_bit_3_carry_out),
    .carry_out(full_adder_4_bit_2_carry_out), .\output (\output [7:4]));
  full_adder_4_bit full_adder_4_bit_3 (
    .input1(in_1[7:4]), .input2(in_2[7:4]), .carry_in(full_adder_4_bit_4_carry_out),
    .carry_out(full_adder_4_bit_3_carry_out), .\output (\output [11:8]));
  full_adder_4_bit full_adder_4_bit_4 (
    .input1(in_1[3:0]), .input2(in_2[3:0]), .carry_in(carry_in), .carry_out(full_adder_4_bit_4_carry_out),
    .\output (\output [15:12]));
endmodule
